// Logisim project TwoIdenticalCircuits.circ as structural Verilog: 1 circuit, main circuit main
module main (
  input  SW_1,
  input  SW_2,
  input  SW_3,
  output out_4,
  output out_5
);

  wire and_2_out, nand_1_out, nor_1_out, or_1_out;

  and and_1 (out_4, SW_1, SW_2, ~SW_3);  // AND_Gate
  and and_2 (and_2_out, SW_1, SW_2);
  or or_1 (or_1_out, and_2_out, nor_1_out);
  nor nor_1 (nor_1_out, ~SW_2, ~SW_3);  // NOR_Gate
  nand nand_1 (nand_1_out, SW_2, SW_3);
  and and_3 (out_5, or_1_out, nand_1_out);
endmodule
