// Logisim project muxFromGates.circ as structural Verilog: 1 circuit, main circuit main
module main (
  input  data_In_1,
  input  data_In_2,
  input  selectLine,
  output \output 
);

  wire and_1_out, and_2_out, not_1_out;

  not not_1 (not_1_out, selectLine);
  and and_1 (and_1_out, data_In_2, selectLine);
  or or_1 (\output , and_1_out, and_2_out);
  and and_2 (and_2_out, data_In_1, not_1_out);
endmodule
