// Logisim project muxFromVoltageControlledBuffers.circ as structural Verilog: 1 circuit, main circuit main
module main (
  input  data_in_1,
  input  data_in_2,
  input  select_line,
  output \output 
);

  wire controlled_inverter_1_out;

  assign controlled_inverter_1_out = select_line ? ~select_line : 1'bz;  // Controlled_Inverter controlled_inverter_1
  Pull_Resistor #(.pull(1)) pull_resistor_1 (.node(\output ));
  assign \output  = select_line ? data_in_1 : 1'bz;  // Controlled_Buffer controlled_buffer_1
  assign \output  = controlled_inverter_1_out ? data_in_2 : 1'bz;  // Controlled_Buffer controlled_buffer_2
  Pull_Resistor #(.pull(1)) pull_resistor_2 (.node(controlled_inverter_1_out));
endmodule
