// Logisim project TestingMuxWithDecoder.circ as structural Verilog: 1 circuit, main circuit main
module main (
  input  [1:0] in_1
);

  wire decoder_1_out0, decoder_1_out1, decoder_1_out2, decoder_1_out3, multiplexer_1_out;

  Decoder #(.select(2), .enable("false")) decoder_1 (
    .out0(decoder_1_out0), .out1(decoder_1_out1), .out2(decoder_1_out2), .out3(decoder_1_out3), .sel(in_1));
  Multiplexer #(.select(2), .enable("false")) multiplexer_1 (
    .in0(decoder_1_out0), .in1(decoder_1_out1), .in2(decoder_1_out2), .in3(decoder_1_out3),
    .out(multiplexer_1_out), .sel(in_1));
endmodule
