// Logisim project EveryOtherClocked.circ as structural Verilog: 1 circuit, main circuit main
module main (
  input  y1,
  input  in_2,
  input  y2,
  output out_4
);

  wire and_1_out, and_2_out, and_3_out, or_1_out, or_2_out;

  and and_1 (and_1_out, y1, in_2);
  and and_2 (and_2_out, ~in_2, y2);  // AND_Gate
  and and_3 (and_3_out, in_2, ~y1);  // AND_Gate
  or or_1 (or_1_out, and_1_out, and_2_out);
  or or_2 (or_2_out, and_2_out, and_3_out);
  and and_4 (out_4, ~or_1_out, or_2_out);  // AND_Gate

  // Notes on the sheet:
  //   from http://pami.uwaterloo.ca/~basir/ECE124/Asynchronous_Sequential.pdf
  //   drag gray feed back lines into place, disconnect top and bottom switches y1 and y2
  //   feed back or delay  line #1
  //   feed back or delay line #2
  //   Y1
  //   Y2
endmodule
