// Logisim project ComboLockDone.circ as structural Verilog: 3 circuits, main circuit Main
module ASN (
  input  y1,
  input  y2,
  input  y3,
  input  y4,
  input  y5,
  input  E,
  input  S,
  output Y1_2,
  output Y2_2,
  output Y3_2,
  output Y4_2,
  output Y5_2,
  output Z
);

  wire and_1_out, and_2_out, and_3_out, and_4_out, and_5_out, and_6_out, and_7_out, and_8_out, and_9_out,
       and_10_out, and_11_out, and_12_out, and_13_out, and_14_out, and_15_out, and_16_out, and_17_out,
       and_18_out, not_1_out, not_2_out, not_3_out, not_4_out, not_5_out, not_6_out, not_7_out, not_8_out,
       not_9_out, not_10_out, not_11_out, not_12_out, not_13_out, not_14_out, not_15_out;

  and and_1 (and_1_out, y4, y5, E, S);
  and and_2 (and_2_out, y1, S);
  and and_3 (and_3_out, y1, E);
  not not_1 (not_1_out, y3);
  not not_2 (not_2_out, E);
  not not_3 (not_3_out, E);
  not not_4 (not_4_out, E);
  not not_5 (not_5_out, y2);
  not not_6 (not_6_out, y5);
  not not_7 (not_7_out, y1);
  not not_8 (not_8_out, E);
  not not_9 (not_9_out, S);
  not not_10 (not_10_out, y2);
  not not_11 (not_11_out, E);
  not not_12 (not_12_out, E);
  not not_13 (not_13_out, S);
  and and_4 (and_4_out, y1, S);
  and and_5 (and_5_out, y1, E);
  or or_1 (Y1_2, and_1_out, and_2_out, and_3_out);
  and and_6 (and_6_out, not_1_out, not_2_out, S);
  and and_7 (and_7_out, y2, E, S);
  and and_8 (and_8_out, y2, y5, not_3_out);
  not not_14 (not_14_out, y5);
  not not_15 (not_15_out, S);
  and and_9 (and_9_out, y3, not_4_out);
  and and_10 (and_10_out, not_5_out, not_6_out, E, S);
  and and_11 (and_11_out, y4, S);
  and and_12 (and_12_out, not_7_out, y4, y5, not_8_out);
  and and_13 (and_13_out, y1, E);
  and and_14 (and_14_out, E, not_9_out);
  and and_15 (and_15_out, not_10_out, y5);
  and and_16 (and_16_out, y5, not_11_out);
  and and_17 (and_17_out, y4, not_12_out);
  and and_18 (and_18_out, y2, not_13_out);
  or or_2 (Z, and_4_out, and_5_out);
  or or_3 (Y2_2, and_6_out, and_7_out, and_8_out);
  or or_4 (Y3_2, not_14_out, not_15_out, y4, and_9_out, y2);
  or or_5 (Y4_2, and_10_out, and_11_out, and_12_out, and_13_out);
  or or_6 (Y5_2, and_14_out, and_15_out, and_16_out, and_17_out, and_18_out);
endmodule

module Main (
  input  [3:0] combo_00,
  input  [3:0] combo_01,
  input  [3:0] combo_10,
  input  [3:0] combo_11,
  input  enter,
  input  [3:0] in_6,
  input  start_switch,
  output combination_num,
  output out_9,
  output _0___locked__1___unlocked
);

  wire asn_1_y1_2, asn_1_y2_2, asn_1_y3_2, asn_1_y4_2, asn_1_y5_2;
  wire [3:0] multiplexer_1_out, xnor_1_out;

  assign xnor_1_out = ~(multiplexer_1_out ^ in_6);  // XNOR_Gate xnor_1, 4 bits wide
  // AND_Gate passFail has open pins: in0=xnor_1_out[0], in1=xnor_1_out[1], in2=xnor_1_out[2], in3=xnor_1_out[3], out=open
  ASN asn_1 (
    .y1(asn_1_y1_2), .y2(asn_1_y2_2), .y3(asn_1_y3_2), .y4(asn_1_y4_2), .y5(asn_1_y5_2), .E(enter),
    .S(start_switch), .Y1_2(asn_1_y1_2), .Y2_2(asn_1_y2_2), .Y3_2(asn_1_y3_2), .Y4_2(asn_1_y4_2),
    .Y5_2(asn_1_y5_2), .Z(_0___locked__1___unlocked));
  Multiplexer #(.select(2), .width(4), .enable("false")) multiplexer_1 (
    .in0(combo_00), .in1(combo_01), .in2(combo_10), .in3(combo_11), .out(multiplexer_1_out),
    .sel({combination_num, out_9}));
  ComboCombinatory combocombinatory_1 (
    .y1(asn_1_y1_2), .y2(asn_1_y2_2), .y3(asn_1_y3_2), .y4(asn_1_y4_2), .y5(asn_1_y5_2),
    .s1(combination_num), .s2(out_9));

  // Notes on the sheet:
  //   correct combinations
  //   To get started, bang on start switch and enter until green
  //   Then disconnect start switch and hook up four input and gate
  //   looking for
endmodule

// Combo
module ComboCombinatory (
  input  y1,
  input  y2,
  input  y3,
  input  y4,
  input  y5,
  output s1,
  output s2
);

  wire and_1_out, and_2_out, not_1_out, not_2_out;

  not not_1 (not_1_out, y2);
  not not_2 (not_2_out, y5);
  and and_1 (and_1_out, y4, y5);
  and and_2 (and_2_out, not_1_out, not_2_out);
  or or_1 (s2, and_1_out, y2);
  or or_2 (s1, and_2_out, y4);

  // Notes on the sheet:
  //   Obviously Logisim can not reduce this the ASN
  //   anymore than Logisim can reduce a clocked flip flop network
endmodule
