// Logisim project Hw1.circ as structural Verilog: 1 circuit, main circuit main
module main (
  input  A,
  input  B,
  input  C,
  output X,
  output Y
);

  wire nand_1_out, not_1_out, xor_1_out;

  xor xor_1 (xor_1_out, A, B);
  not not_1 (not_1_out, C);
  not not_2 (X, xor_1_out);
  nand nand_1 (nand_1_out, xor_1_out, C);
  or or_1 (Y, nand_1_out, not_1_out);
endmodule
