// Logisim project HW2 sim.circ as structural Verilog
module Circuit_X (
  input  A,
  input  B,
  input  C,
  output X
);

  wire nand_1_out, not_1_out, or_1_out, xor_1_out, xor_2_out;

  not not_1 (not_1_out, A);
  xor xor_1 (xor_1_out, not_1_out, B);
  or or_1 (or_1_out, B, A);
  nand nand_1 (nand_1_out, xor_1_out, C);
  xor xor_2 (xor_2_out, C, or_1_out);
  or or_2 (X, nand_1_out, xor_2_out);
endmodule

module Circuit_Y (
  input  D,
  input  E,
  input  F,
  output Y
);

  wire and_1_out, nor_1_out, not_1_out, not_2_out, or_1_out, xnor_1_out;

  xnor xnor_1 (xnor_1_out, D, E);
  and and_1 (and_1_out, F, D);
  not not_1 (not_1_out, D);
  not not_2 (not_2_out, E);
  nor nor_1 (nor_1_out, xnor_1_out, and_1_out);
  or or_1 (or_1_out, not_1_out, not_2_out);
  and and_2 (Y, nor_1_out, or_1_out);
endmodule
