// Logisim project Hw1_3.circ as structural Verilog: 2 circuits, main circuit main
module main (
  input  A,
  input  B,
  input  C,
  output X,
  output Y
);

  wire nand_1_out, not_1_out, xor_1_out;

  xor xor_1 (xor_1_out, A, B);
  not not_1 (not_1_out, C);
  not not_2 (X, xor_1_out);
  nand nand_1 (nand_1_out, xor_1_out, C);
  or or_1 (Y, nand_1_out, not_1_out);
endmodule

module Hw3 (
  input  A,
  input  B,
  input  C,
  output X,
  output Y
);

  wire nor_1_out, xor_1_out;

  xor xor_1 (xor_1_out, A, B);
  not not_1 (X, xor_1_out);
  nor nor_1 (nor_1_out, ~xor_1_out, ~C);  // NOR_Gate
  nand nand_1 (Y, nor_1_out, C);
endmodule
