// Logisim project circuitToKmap.circ as structural Verilog
module Circuit_X (
  input  W,
  input  X,
  input  Y,
  input  Z,
  output X_2
);

  wire and_1_out, nand_1_out, or_1_out, or_2_out, xor_1_out;

  or or_1 (or_1_out, W, X);
  and and_1 (and_1_out, Y, Z);
  or or_2 (or_2_out, or_1_out, Y);
  xor xor_1 (xor_1_out, or_2_out, nand_1_out);
  nand nand_1 (nand_1_out, or_1_out, and_1_out);
  nor nor_1 (X_2, xor_1_out, and_1_out);
endmodule
